// Logisim project t_trigger.circ as structural Verilog: 1 circuit, main circuit main
module main (
  input  in_1,
  output [2:0] out_2
);

  wire and_1_out, t_ff_2_qn, t_ff_3_qn;

  and and_1 (and_1_out, t_ff_3_qn, t_ff_2_qn);
  T_Flip_Flop t_ff_1 (.T(and_1_out), .clk(in_1), .Q(out_2[2]));  // open: Qn, reset, preset
  T_Flip_Flop t_ff_2 (.T(t_ff_3_qn), .clk(in_1), .Q(out_2[1]), .Qn(t_ff_2_qn));  // open: reset, preset
  T_Flip_Flop t_ff_3 (.T(in_1), .clk(in_1), .Q(out_2[0]), .Qn(t_ff_3_qn));  // open: reset, preset
endmodule
